# Fritzing sketch sensor (saved by Fritzing 0.9.3b)
breadboards: 1

parts:
  K1 = Relay [part_number=FRS1B-S package=THT]
  R3 = Resistor [tolerance=±5% resistance=300k package=THT]
  Q1 = NPN-Transistor [package="TO92 [THT]"]
  D1 = Rectifier Diode [part_number=1N4001 package="300 mil [THT]"]
  IC1 = DIP - 8 pins [part_number=LM741 package="DIP (Dual Inline) [THT]"]
  C1 = Ceramic Capacitor [capacitance=1µF package="100 mil [THT, multilayer]"]
  R2 = Resistor [tolerance=±5% resistance=100k package=THT]
  R1 = Resistor [tolerance=±5% resistance=100k package=THT]
  R4 = Resistor [tolerance=±5% resistance=1M package=THT]
  S1 = Pushbutton [package=THT]
  S2 = Pushbutton [package=THT]
  IC2 = Voltage Regulator [package=to-220-alt]
  C2 = Ceramic Capacitor [capacitance=100nF package="100 mil [THT, multilayer]"]
  C3 = Ceramic Capacitor [capacitance=100nF package="100 mil [THT, multilayer]"]
  U1 = Transformer [package=transformer_smd]
  D2 = Diode [package=sma-diode]
  D3 = Diode [package=sma-diode]
  D4 = Diode [package=sma-diode]
  D5 = Diode [package=sma-diode]

nets:
  N1: K1.COIL1, Q1.C, D1.cathode
  N2: K1.C1, K1.C2, U1.2
  N3: K1.COIL2, D1.anode, IC1.pin7, C1.1, R2.Pin_0, S1.leg0, IC2.OUT, C3.1
  N4: R3.Pin_0, IC1.pin6
  N5: R3.Pin_1, Q1.B
  N6: Q1.E, IC1.pin4, R1.Pin_0, S1.leg1, IC2.GND, C2.0, C3.0, D3.A, D5.A
  N7: IC1.pin2, C1.0, R4.Pin_1
  N8: IC1.pin3, R2.Pin_1, R1.Pin_1
  N9: S2.leg1, U1.1
  N10: IC2.IN, C2.1, D2.C, D4.C
  N11: U1.3, D4.A, D5.C
  N12: U1.4, D2.A, D3.C

custom parts:
  DIP - 8 pins: A DIP stand-in part for whatever IC you want. With 8 pins on a 300 mil dual inline package (DIP) footprint.
